// Logisim project FourBitParity.circ as structural Verilog: 2 circuits, main circuit implementation
module implementation (
  input  EnableIn,
  input  InputBitIn,
  input  ClkIn,
  output IsEvenOut
);

  wire [2:0] register_1_q, state_calc_new_state;

  Register #(.width(3)) register_1 (
    .D(state_calc_new_state), .en(EnableIn), .clk(ClkIn), .Q(register_1_q));  // open: clr
  next_state_calc state_calc (.old_state(register_1_q), .new_input(InputBitIn), .new_state(state_calc_new_state));
  and and_1 (IsEvenOut, register_1_q[2], register_1_q[1], ~register_1_q[0]);  // AND_Gate

  // Other names for the same wires on the sheet: Clk = ClkIn; Enable = EnableIn; even_num_ones = IsEvenOut;
  //   InputBit = InputBitIn

  // Notes on the sheet:
  //   Feed next state back into register
  //   Only have even number of ones for exactly one state, 110
  //   Tom Kwon and Martin Orosa
endmodule

module next_state_calc (
  input  [2:0] old_state,
  input  new_input,
  output [2:0] new_state
);

  wire and_1_out, and_2_out, and_3_out, and_4_out, and_5_out, and_6_out, and_7_out, and_8_out, and_9_out,
       and_10_out, and_11_out, and_12_out, not_1_out, not_2_out, not_3_out, not_4_out;

  not not_1 (not_1_out, old_state[2]);
  not not_2 (not_2_out, old_state[1]);
  not not_3 (not_3_out, old_state[0]);
  not not_4 (not_4_out, new_input);
  and and_1 (and_1_out, not_2_out, not_3_out, not_4_out);
  and and_2 (and_2_out, not_1_out, old_state[0], new_input);
  and and_3 (and_3_out, not_1_out, old_state[1], new_input);
  and and_4 (and_4_out, old_state[2], not_4_out);
  and and_5 (and_5_out, old_state[0], not_4_out);
  and and_6 (and_6_out, not_1_out, old_state[1], new_input);
  and and_7 (and_7_out, old_state[2], not_2_out, new_input);
  and and_8 (and_8_out, not_1_out, not_2_out, new_input);
  and and_9 (and_9_out, not_1_out, not_2_out, old_state[0]);
  and and_10 (and_10_out, not_1_out, old_state[0], new_input);
  and and_11 (and_11_out, old_state[2], not_2_out, not_4_out);
  and and_12 (and_12_out, old_state[2], not_3_out, new_input);
  or or_1 (new_state[2], and_1_out, and_2_out, and_3_out, and_4_out);
  or or_2 (new_state[1], and_5_out, and_6_out, and_7_out);
  or or_3 (new_state[0], and_8_out, and_9_out, and_10_out, and_11_out, and_12_out);
endmodule
