// Logisim project UpDownCounter.circ as structural Verilog: 4 circuits, main circuit implementation
module implementation (
  input  EnableIn,
  input  CountUpIn,
  input  CountDownIn,
  input  clkIn,
  output [2:0] out_5
);

  wire d0_1_d0bit, d1_1_d1bit, d2_1_d2bit;

  D2 d2_1 (.Q2(out_5[2]), .Q1(out_5[1]), .Q0(out_5[0]), .Up(CountUpIn), .Down(CountDownIn), .D2bit(d2_1_d2bit));
  D1 d1_1 (.Q2(out_5[2]), .Q1(out_5[1]), .Q0(out_5[0]), .Up(CountUpIn), .Down(CountDownIn), .D1bit(d1_1_d1bit));
  D0 d0_1 (.Q2(out_5[2]), .Q1(out_5[1]), .Q0(out_5[0]), .Up(CountUpIn), .Down(CountDownIn), .D0bit(d0_1_d0bit));
  Register #(.width(1)) register_1 (.D(d2_1_d2bit), .en(EnableIn), .clk(clkIn), .Q(out_5[2]));  // open: clr
  Register #(.width(1)) register_2 (.D(d1_1_d1bit), .en(EnableIn), .clk(clkIn), .Q(out_5[1]));  // open: clr
  Register #(.width(1)) register_3 (.D(d0_1_d0bit), .en(EnableIn), .clk(clkIn), .Q(out_5[0]));  // open: clr

  // Other names for the same wires on the sheet: clk = clkIn; count[2:0] = out_5; Q0 = out_5[0]; Q1 = out_5[1];
  //   Q2 = out_5[2]; CountDown = CountDownIn; CountUp = CountUpIn; Enable = EnableIn

  // Notes on the sheet:
  //   Tom Kwon
  //   Martin Orosa
endmodule

module D2 (
  input  Q2,
  input  Q1,
  input  Q0,
  input  Up,
  input  Down,
  output D2bit
);

  wire and_1_out, and_2_out, and_3_out, and_4_out, and_5_out, not_1_out, not_2_out, not_3_out, not_4_out,
       not_5_out, not_6_out, not_7_out, not_8_out;

  not not_1 (not_1_out, Q0);
  not not_2 (not_2_out, Up);
  not not_3 (not_3_out, Q0);
  not not_4 (not_4_out, Up);
  not not_5 (not_5_out, Down);
  not not_6 (not_6_out, Down);
  not not_7 (not_7_out, Down);
  not not_8 (not_8_out, Up);
  and and_1 (and_1_out, Q2, Q1, not_1_out, not_2_out);
  and and_2 (and_2_out, Q2, not_3_out, not_4_out, not_5_out);
  and and_3 (and_3_out, Q1, Q0, Up, not_6_out);
  and and_4 (and_4_out, Q2, Up, not_7_out);
  and and_5 (and_5_out, Q2, Q0, not_8_out);
  or or_1 (D2bit, and_1_out, and_2_out, and_3_out, and_4_out, and_5_out);
endmodule

module D1 (
  input  Q2,
  input  Q1,
  input  Q0,
  input  Up,
  input  Down,
  output D1bit
);

  wire and_1_out, and_2_out, and_3_out, and_4_out, and_5_out, and_6_out, not_1_out, not_2_out, not_3_out,
       not_4_out, not_5_out, not_6_out, not_7_out, not_8_out, not_9_out, not_10_out, not_11_out, not_12_out;

  not not_1 (not_1_out, Q1);
  not not_2 (not_2_out, Q1);
  not not_3 (not_3_out, Q0);
  not not_4 (not_4_out, Up);
  not not_5 (not_5_out, Down);
  not not_6 (not_6_out, Q0);
  not not_7 (not_7_out, Up);
  not not_8 (not_8_out, Q0);
  not not_9 (not_9_out, Down);
  not not_10 (not_10_out, Down);
  not not_11 (not_11_out, Down);
  not not_12 (not_12_out, Up);
  and and_1 (and_1_out, Q1, not_3_out, not_4_out, not_5_out);
  and and_2 (and_2_out, Q2, Down, not_1_out, not_6_out, not_7_out);
  and and_3 (and_3_out, Q1, not_8_out, not_9_out, Up);
  and and_4 (and_4_out, not_2_out, not_10_out, Q0, Up);
  and and_5 (and_5_out, Q2, Q0, Up, not_11_out);
  and and_6 (and_6_out, not_12_out, Q0, Q1);
  or or_1 (D1bit, and_1_out, and_2_out, and_3_out, and_4_out, and_5_out, and_6_out);
endmodule

module D0 (
  input  Q2,
  input  Q1,
  input  Q0,
  input  Up,
  input  Down,
  output D0bit
);

  wire and_1_out, and_2_out, and_3_out, and_4_out, and_5_out, not_1_out, not_2_out, not_3_out, not_4_out,
       not_5_out, not_6_out, not_7_out, not_8_out, not_9_out;

  not not_1 (not_1_out, Up);
  not not_2 (not_2_out, Q0);
  not not_3 (not_3_out, Q0);
  not not_4 (not_4_out, Up);
  not not_5 (not_5_out, Q0);
  not not_6 (not_6_out, Down);
  not not_7 (not_7_out, Down);
  not not_8 (not_8_out, Up);
  not not_9 (not_9_out, Down);
  and and_1 (and_1_out, Q1, not_1_out, not_2_out, Down);
  and and_2 (and_2_out, Q2, not_3_out, not_4_out, Down);
  and and_3 (and_3_out, Up, not_5_out, not_6_out);
  and and_4 (and_4_out, not_7_out, Q2, Q1, Up);
  and and_5 (and_5_out, not_8_out, Q0, not_9_out);
  or or_1 (D0bit, and_1_out, and_2_out, and_3_out, and_4_out, and_5_out);
endmodule
