// Logisim project Vending.circ as structural Verilog: 3 circuits, main circuit implementation
module implementation (
  input  EnableIn,
  input  QuarterReceivedIn,
  input  DimeReceivedIn,
  input  NickelReceivedIn,
  input  ClkIn,
  output Give_Mechandise_Out,
  output Give_Dime_Out,
  output Give_Nickel_Out
);

  wire [2:0] calc_next_state_new_state, register_1_q;

  Register #(.width(3)) register_1 (
    .D(calc_next_state_new_state), .en(EnableIn), .clk(ClkIn), .Q(register_1_q));  // open: clr
  // Probe on calc_next_state_new_state
  // Probe on register_1_q
  next_state_calc calc_next_state (
    .old_state(register_1_q), .input_bits({QuarterReceivedIn, DimeReceivedIn, NickelReceivedIn}),
    .new_state(calc_next_state_new_state));
  output_calc calc_output (
    .old_state(register_1_q), .input_bits({QuarterReceivedIn, DimeReceivedIn, NickelReceivedIn}),
    .output_bits({Give_Dime_Out, Give_Nickel_Out, Give_Mechandise_Out}));

  // Other names for the same wires on the sheet: Give_Merchandise = Give_Mechandise_Out;
  //   Give_Nickel = Give_Nickel_Out; Give_Dime = Give_Dime_Out; clk = ClkIn; Enable = EnableIn;
  //   input_bits[2:0] = {QuarterReceivedIn, DimeReceivedIn, NickelReceivedIn}; NickelReceieved = NickelReceivedIn;
  //   DimeReceieved = DimeReceivedIn; QuarterReceieved = QuarterReceivedIn

  // Notes on the sheet:
  //   Current state
  //   Tom Kwon and Martin Orosa
  //   Next state
endmodule

module next_state_calc (
  input  [2:0] old_state,
  input  [2:0] input_bits,
  output [2:0] new_state
);

  wire and_1_out, and_2_out, and_3_out, and_4_out, and_5_out, and_6_out, and_7_out, and_8_out, and_9_out,
       and_10_out, and_11_out, and_12_out, and_13_out, not_1_out, not_2_out, not_3_out, not_4_out, not_5_out,
       not_6_out;

  not not_1 (not_1_out, old_state[2]);
  not not_2 (not_2_out, old_state[1]);
  not not_3 (not_3_out, old_state[0]);
  not not_4 (not_4_out, input_bits[2]);
  not not_5 (not_5_out, input_bits[1]);
  not not_6 (not_6_out, input_bits[0]);
  and and_1 (and_1_out, not_1_out, not_2_out, not_3_out, input_bits[2]);
  and and_2 (and_2_out, old_state[1], input_bits[1]);
  and and_3 (and_3_out, old_state[1], old_state[0], input_bits[0]);
  and and_4 (and_4_out, old_state[2], not_4_out, not_5_out, not_6_out);
  and and_5 (and_5_out, old_state[2], not_3_out, input_bits[0]);
  and and_6 (and_6_out, not_1_out, not_2_out, input_bits[1]);
  and and_7 (and_7_out, not_1_out, not_2_out, old_state[0], input_bits[0]);
  and and_8 (and_8_out, old_state[1], not_4_out, not_5_out, not_6_out);
  and and_9 (and_9_out, old_state[1], not_3_out, input_bits[0]);
  and and_10 (and_10_out, not_3_out, input_bits[0]);
  and and_11 (and_11_out, not_1_out, not_2_out, not_3_out, input_bits[2]);
  and and_12 (and_12_out, not_1_out, old_state[0], not_4_out, not_6_out);
  and and_13 (and_13_out, old_state[0], not_4_out, not_5_out, not_6_out);
  or or_1 (new_state[2], and_1_out, and_2_out, and_3_out, and_4_out, and_5_out);
  or or_2 (new_state[1], and_6_out, and_7_out, and_8_out, and_9_out);
  or or_3 (new_state[0], and_10_out, and_11_out, and_12_out, and_13_out);
endmodule

module output_calc (
  input  [2:0] old_state,
  input  [2:0] input_bits,
  output [2:0] output_bits
);

  wire and_1_out, and_2_out, and_3_out, and_4_out, and_5_out, and_6_out, and_7_out, and_8_out, and_9_out,
       and_10_out, not_1_out;

  not not_1 (not_1_out, old_state[0]);
  and and_1 (and_1_out, old_state[1], old_state[0], input_bits[2]);
  and and_2 (and_2_out, old_state[2], input_bits[2]);
  and and_3 (and_3_out, old_state[1], not_1_out, input_bits[2]);
  and and_4 (and_4_out, old_state[2], input_bits[2]);
  and and_5 (and_5_out, old_state[2], old_state[0], input_bits[1]);
  and and_6 (and_6_out, old_state[0], input_bits[2]);
  and and_7 (and_7_out, old_state[1], input_bits[2]);
  and and_8 (and_8_out, old_state[2], input_bits[1]);
  and and_9 (and_9_out, old_state[2], input_bits[2]);
  and and_10 (and_10_out, old_state[2], old_state[0], input_bits[0]);
  or or_1 (output_bits[2], and_1_out, and_2_out);
  or or_2 (output_bits[1], and_3_out, and_4_out, and_5_out);
  or or_3 (output_bits[0], and_6_out, and_7_out, and_8_out, and_9_out, and_10_out);
endmodule
